// Logisim project Gekko.circ as structural Verilog: 8 circuits, main circuit main
module main (
);

  IU2 IU2_1 ();  // open: XER, Opcode, A, B, XERBits
  Register #(.width(32)) XER ();  // open: D, en, clk, Q, clr
  Register #(.width(32)) CR ();  // open: D, en, clk, Q, clr
  GPRFile GPRFile_1 ();  // open: WriteReg, WriteValue, ReadReg1, ReadReg2, Reg1Value, Reg2Value
  FPRFile FPRFile_1 ();
  FPU FPU_1 ();  // open: A, B

  // Notes on the sheet:
  //   32-Bit Address Bus
endmodule

module IU2 (
  input  [31:0] XER,
  input  [31:0] Opcode,
  input  [31:0] A,
  input  [31:0] B,
  output [2:0] XERBits
);

  wire bitselector_1_out;

  BitSelector #(.width(32)) bitselector_1 (.in(XER), .out(bitselector_1_out), .sel(5'b00010));
  IUFastAdderComparator IUFastAdderComparator_1 (
    .Cin(bitselector_1_out), .A(A), .B(B));  // open: Sum, Cout, Greater, Equal, Less
  IULogic IULogic_1 (.A(A), .B(B));  // open: ands, ors, xors
  IUShiftsRotatesCountLeadingZeros IUShiftsRotatesCountLeadingZeros_1 (
    .A(A), .B(B));  // open: RotateLeft, LogicalLeft, LogicalRight, AlgebraicRight
endmodule

module IUFastAdderComparator (
  input  Cin,
  input  [31:0] A,
  input  [31:0] B,
  output [31:0] Sum,
  output Cout,
  output Greater,
  output Equal,
  output Less
);

  Adder #(.width(32)) adder_1 (.a(A), .b(B), .out(Sum), .cin(Cin), .cout(Cout));
  Comparator #(.width(32)) comparator_1 (.a(A), .b(B), .gt(Greater), .eq(Equal), .lt(Less));
endmodule

module IULogic (
  input  [31:0] A,
  input  [31:0] B,
  output [31:0] ands,
  output [31:0] ors,
  output [31:0] xors
);

  assign ands = A & B;  // AND_Gate and_1, 32 bits wide
  assign ors = A | B;  // OR_Gate or_1, 32 bits wide
  assign xors = A ^ B;  // XOR_Gate xor_1, 32 bits wide
endmodule

module IUShiftsRotatesCountLeadingZeros (
  input  [31:0] A,
  input  [31:0] B,
  output [31:0] RotateLeft,
  output [31:0] LogicalLeft,
  output [31:0] LogicalRight,
  output [31:0] AlgebraicRight
);

  Shifter #(.shift("rl"), .width(32)) shifter_1 (.in(A));  // open: dist, out
  Shifter #(.width(32)) shifter_2 ();  // open: in, dist, out
  Shifter #(.shift("lr"), .width(32)) shifter_3 ();  // open: in, dist, out
  Shifter #(.shift("ar"), .width(32)) shifter_4 ();  // open: in, dist, out
endmodule

module FPU (
  input  [63:0] A,
  input  [63:0] B
);

  FPAdder fpadder_1 ();  // open: a, b, out
  FPAdder #(.fpwidth(64)) fpadder_2 (.a(A), .b(B));  // open: out
endmodule

module GPRFile (
  input  [4:0] WriteReg,
  input  [31:0] WriteValue,
  input  [4:0] ReadReg1,
  input  [4:0] ReadReg2,
  output [31:0] Reg1Value,
  output [31:0] Reg2Value
);

  wire Clock, EnableGPR0, EnableGPR1, EnableGPR2, EnableGPR3, EnableGPR4, EnableGPR5, EnableGPR6, EnableGPR7,
       EnableGPR8, EnableGPR9, EnableGPR10, EnableGPR11, EnableGPR12, EnableGPR13, EnableGPR14, EnableGPR15,
       EnableGPR16, EnableGPR17, EnableGPR18, EnableGPR19, EnableGPR20, EnableGPR21, EnableGPR22,
       EnableGPR23, EnableGPR24, EnableGPR25, EnableGPR26, EnableGPR27, EnableGPR28, EnableGPR29,
       EnableGPR30, EnableGPR31, undriven, undriven_2, undriven_3, undriven_4, undriven_5, undriven_6,
       undriven_7, undriven_8, undriven_9, undriven_10, undriven_11, undriven_12, undriven_13, undriven_14,
       undriven_15, undriven_16, undriven_17, undriven_18, undriven_19, undriven_20;
  wire [31:0] GPR0, GPR1, GPR2, GPR3, GPR4, GPR5, GPR6, GPR7, GPR8, GPR9, GPR10, GPR11, GPR12, GPR13, GPR14,
       GPR15, GPR16, GPR17, GPR18, GPR19, GPR20, GPR21, GPR22, GPR23, GPR24, GPR25, GPR26, GPR27, GPR28,
       GPR29, GPR30, GPR31;

  Clock clock_1 (.out(Clock));
  Decoder #(.select(5)) decoder_1 (
    .out0(EnableGPR0), .out1(EnableGPR1), .out2(EnableGPR2), .out3(EnableGPR3), .out4(EnableGPR4),
    .out5(EnableGPR5), .out6(EnableGPR6), .out7(EnableGPR7), .out8(EnableGPR8), .out9(EnableGPR9),
    .out10(EnableGPR10), .out11(EnableGPR11), .out12(EnableGPR12), .out13(EnableGPR13), .out14(EnableGPR14),
    .out15(EnableGPR15), .out16(EnableGPR16), .out17(EnableGPR17), .out18(EnableGPR18), .out19(EnableGPR19),
    .out20(EnableGPR20), .out21(EnableGPR21), .out22(EnableGPR22), .out23(EnableGPR23), .out24(EnableGPR24),
    .out25(EnableGPR25), .out26(EnableGPR26), .out27(EnableGPR27), .out28(EnableGPR28), .out29(EnableGPR29),
    .out30(EnableGPR30), .out31(EnableGPR31), .sel(WriteReg));  // open: en
  Multiplexer #(.select(5), .width(32)) multiplexer_1 (
    .in0(GPR0), .in1(GPR1), .in2(GPR2), .in3(GPR3), .in4(GPR4), .in5(GPR5), .in6(GPR6), .in7(GPR7),
    .in8(GPR8), .in9(GPR9), .in10(GPR10), .in11(GPR11), .in12(GPR12), .in13(GPR13), .in14(GPR14),
    .in15(GPR15), .in16(GPR16), .in17(GPR17), .in18(GPR18), .in19(GPR19), .in20(GPR20), .in21(GPR21),
    .in22(GPR22), .in23(GPR23), .in24(GPR24), .in25(GPR25), .in26(GPR26), .in27(GPR27), .in28(GPR28),
    .in29(GPR29), .in30(GPR30), .in31(GPR31), .out(Reg1Value), .sel(ReadReg1));
  Multiplexer #(.select(5), .width(32)) multiplexer_2 (
    .in0(GPR0), .in1(GPR1), .in2(GPR2), .in3(GPR3), .in4(GPR4), .in5(GPR5), .in6(GPR6), .in7(GPR7),
    .in8(GPR8), .in9(GPR9), .in10(GPR10), .in11(GPR11), .in12(GPR12), .in13(GPR13), .in14(GPR14),
    .in15(GPR15), .in16(GPR16), .in17(GPR17), .in18(GPR18), .in19(GPR19), .in20(GPR20), .in21(GPR21),
    .in22(GPR22), .in23(GPR23), .in24(GPR24), .in25(GPR25), .in26(GPR26), .in27(GPR27), .in28(GPR28),
    .in29(GPR29), .in30(GPR30), .in31(GPR31), .out(Reg2Value), .sel(ReadReg2));
  Register #(.width(32)) u_GPR0 (.D(WriteValue), .en(EnableGPR0), .clk(Clock), .Q(GPR0));  // open: clr
  Register #(.width(32)) u_GPR1 (.D(WriteValue), .en(EnableGPR1), .clk(Clock), .Q(GPR1));  // open: clr
  Register #(.width(32)) u_GPR2 (.D(WriteValue), .en(EnableGPR2), .clk(Clock), .Q(GPR2));  // open: clr
  Register #(.width(32)) u_GPR3 (.D(WriteValue), .en(EnableGPR3), .clk(Clock), .Q(GPR3));  // open: clr
  Register #(.width(32)) u_GPR4 (.D(WriteValue), .en(EnableGPR4), .clk(Clock), .Q(GPR4));  // open: clr
  Register #(.width(32)) u_GPR5 (.D(WriteValue), .en(EnableGPR5), .clk(Clock), .Q(GPR5));  // open: clr
  Register #(.width(32)) u_GPR6 (.D(WriteValue), .en(EnableGPR6), .clk(Clock), .Q(GPR6));  // open: clr
  Register #(.width(32)) u_GPR7 (.D(WriteValue), .en(EnableGPR7), .clk(Clock), .Q(GPR7));  // open: clr
  Register #(.width(32)) u_GPR8 (.D(WriteValue), .en(EnableGPR8), .clk(Clock), .Q(GPR8));  // open: clr
  Register #(.width(32)) u_GPR9 (.D(WriteValue), .en(EnableGPR9), .clk(Clock), .Q(GPR9));  // open: clr
  Register #(.width(32)) u_GPR10 (.D(WriteValue), .en(EnableGPR10), .clk(Clock), .Q(GPR10));  // open: clr
  Register #(.width(32)) u_GPR11 (.D(WriteValue), .en(EnableGPR11), .clk(Clock), .Q(GPR11));  // open: clr
  Register #(.width(32)) u_GPR12 (.D(WriteValue), .en(EnableGPR12), .clk(undriven), .Q(GPR12));  // open: clr
  Register #(.width(32)) u_GPR13 (.D(WriteValue), .en(EnableGPR13), .clk(undriven_2), .Q(GPR13));  // open: clr
  Register #(.width(32)) u_GPR14 (.D(WriteValue), .en(EnableGPR14), .clk(undriven_3), .Q(GPR14));  // open: clr
  Register #(.width(32)) u_GPR15 (.D(WriteValue), .en(EnableGPR15), .clk(undriven_4), .Q(GPR15));  // open: clr
  Register #(.width(32)) u_GPR16 (.D(WriteValue), .en(EnableGPR16), .clk(undriven_5), .Q(GPR16));  // open: clr
  Register #(.width(32)) u_GPR17 (.D(WriteValue), .en(EnableGPR17), .clk(undriven_6), .Q(GPR17));  // open: clr
  Register #(.width(32)) u_GPR18 (.D(WriteValue), .en(EnableGPR18), .clk(undriven_7), .Q(GPR18));  // open: clr
  Register #(.width(32)) u_GPR19 (.D(WriteValue), .en(EnableGPR19), .clk(undriven_8), .Q(GPR19));  // open: clr
  Register #(.width(32)) u_GPR20 (.D(WriteValue), .en(EnableGPR20), .clk(undriven_9), .Q(GPR20));  // open: clr
  Register #(.width(32)) u_GPR21 (.D(WriteValue), .en(EnableGPR21), .clk(undriven_10), .Q(GPR21));  // open: clr
  Register #(.width(32)) u_GPR22 (.D(WriteValue), .en(EnableGPR22), .clk(undriven_11), .Q(GPR22));  // open: clr
  Register #(.width(32)) u_GPR23 (.D(WriteValue), .en(EnableGPR23), .clk(undriven_12), .Q(GPR23));  // open: clr
  Register #(.width(32)) u_GPR24 (.D(WriteValue), .en(EnableGPR24), .clk(undriven_13), .Q(GPR24));  // open: clr
  Register #(.width(32)) u_GPR25 (.D(WriteValue), .en(EnableGPR25), .clk(undriven_14), .Q(GPR25));  // open: clr
  Register #(.width(32)) u_GPR26 (.D(WriteValue), .en(EnableGPR26), .clk(undriven_15), .Q(GPR26));  // open: clr
  Register #(.width(32)) u_GPR27 (.D(WriteValue), .en(EnableGPR27), .clk(undriven_16), .Q(GPR27));  // open: clr
  Register #(.width(32)) u_GPR28 (.D(WriteValue), .en(EnableGPR28), .clk(undriven_17), .Q(GPR28));  // open: clr
  Register #(.width(32)) u_GPR29 (.D(WriteValue), .en(EnableGPR29), .clk(undriven_18), .Q(GPR29));  // open: clr
  Register #(.width(32)) u_GPR30 (.D(WriteValue), .en(EnableGPR30), .clk(undriven_19), .Q(GPR30));  // open: clr
  Register #(.width(32)) u_GPR31 (.D(WriteValue), .en(EnableGPR31), .clk(undriven_20), .Q(GPR31));  // open: clr

  // Other names for the same wires on the sheet: WV[31:0] = WriteValue

  // Notes on the sheet:
  //   TODO: How many read/write inputs are there
endmodule

module FPRFile (
);

  Register #(.width(64)) FPR0 ();  // open: D, en, clk, Q, clr
  Register #(.width(64)) FPR1 ();  // open: D, en, clk, Q, clr
  Register #(.width(64)) FPR2 ();  // open: D, en, clk, Q, clr
  Register #(.width(64)) FPR3 ();  // open: D, en, clk, Q, clr
  Register #(.width(64)) FPR4 ();  // open: D, en, clk, Q, clr
  Register #(.width(64)) FPR5 ();  // open: D, en, clk, Q, clr
  Register #(.width(64)) FPR6 ();  // open: D, en, clk, Q, clr
  Register #(.width(64)) FPR7 ();  // open: D, en, clk, Q, clr
  Register #(.width(64)) FPR8 ();  // open: D, en, clk, Q, clr
  Register #(.width(64)) FPR9 ();  // open: D, en, clk, Q, clr
  Register #(.width(64)) FPR10 ();  // open: D, en, clk, Q, clr
  Register #(.width(64)) FPR11 ();  // open: D, en, clk, Q, clr
  Register #(.width(64)) FPR12 ();  // open: D, en, clk, Q, clr
  Register #(.width(64)) FPR13 ();  // open: D, en, clk, Q, clr
  Register #(.width(64)) FPR14 ();  // open: D, en, clk, Q, clr
  Register #(.width(64)) FPR15 ();  // open: D, en, clk, Q, clr
  Register #(.width(64)) FPR16 ();  // open: D, en, clk, Q, clr
  Register #(.width(64)) FPR17 ();  // open: D, en, clk, Q, clr
  Register #(.width(64)) FPR18 ();  // open: D, en, clk, Q, clr
  Register #(.width(64)) FPR19 ();  // open: D, en, clk, Q, clr
  Register #(.width(64)) FPR20 ();  // open: D, en, clk, Q, clr
  Register #(.width(64)) FPR21 ();  // open: D, en, clk, Q, clr
  Register #(.width(64)) FPR22 ();  // open: D, en, clk, Q, clr
  Register #(.width(64)) FPR23 ();  // open: D, en, clk, Q, clr
  Register #(.width(64)) FPR24 ();  // open: D, en, clk, Q, clr
  Register #(.width(64)) FPR25 ();  // open: D, en, clk, Q, clr
  Register #(.width(64)) FPR26 ();  // open: D, en, clk, Q, clr
  Register #(.width(64)) FPR27 ();  // open: D, en, clk, Q, clr
  Register #(.width(64)) FPR28 ();  // open: D, en, clk, Q, clr
  Register #(.width(64)) FPR29 ();  // open: D, en, clk, Q, clr
  Register #(.width(64)) FPR30 ();  // open: D, en, clk, Q, clr
  Register #(.width(64)) FPR31 ();  // open: D, en, clk, Q, clr
endmodule
